// Digital circuit hw3_b.dig as structural Verilog
module hw3_b (
  input  [3:0] X,
  input  [3:0] Y,
  output [3:0] Z
);

  wire comparator_1_eq;
  wire [3:0] add_1_s;

  Comparator #(.Bits(4)) comparator_1 (.a(Y), .b(X), .eq(comparator_1_eq));  // open: gt, lt
  Add #(.Bits(4)) add_1 (.a(X), .b(Y), .c_i(1'b0), .s(add_1_s));  // open: c_o
  Multiplexer #(.Bits(4)) multiplexer_1 (.sel(comparator_1_eq), .in_0(add_1_s), .in_1(Y), .out(Z));
endmodule
